# Fritzing sketch sketch (saved by Fritzing 0.9.4)

parts:
  U1 = ESP32-38PinWide [part_number=ESP32-38PinWide]
  A2 = Waveshare 1.54in epaper display

nets:
  N1: U1.3.3, A2.Pin_1
  N2: U1.GPIO4, A2.Pin_8
  N3: U1.GPIO16, A2.Pin_7
  N4: U1.GPIO17, A2.Pin_6
  N5: U1.GPIO5, A2.Pin_5
  N6: U1.GPIO18, A2.Pin_4
  N7: U1.GPIO23, A2.Pin_3
  N8: U1.GND, A2.Pin_2

notes:
  VCC
  GND
  DIN
  CLK
  CS
  DC
  RST
  BUSY

custom parts:
  ESP32-38PinWide: Generic 38-Pin ESP32 with wide format (only access to one side of pins on a breadboard) based on Stephen Lilley's HiLetgo ESP-WROOM-32 ESP32 ESP-32S Development Board.
  Waveshare 1.54in epaper display: This is an E-Ink display module, 1.54inch, 200x200 resolution, with embedded controller, communicating via SPI interface.
