# Fritzing sketch sketch_XIAO_ESP32C3 (saved by Fritzing 0.9.4)

parts:
  A2 = Waveshare 1.54in epaper display
  A3 = XIAO ESP32C3-tht

nets:
  N1: A2.Pin_1, A3.Pin_20
  N2: A2.Pin_2, A3.Pin_21
  N3: A2.Pin_3, A3.Pin_19
  N4: A2.Pin_4, A3.Pin_17
  N5: A2.Pin_5, A3.Pin_16
  N6: A2.Pin_6, A3.Pin_15
  N7: A2.Pin_7, A3.Pin_10
  N8: A2.Pin_8, A3.Pin_9

notes:
  VCC
  GND
  DIN
  CLK
  CS
  DC
  RST
  BUSY

custom parts:
  Waveshare 1.54in epaper display: This is an E-Ink display module, 1.54inch, 200x200 resolution, with embedded controller, communicating via SPI interface.
  XIAO ESP32C3-tht: Seeed Studio XIAO ESP32C3 adopts new RISC-V architecture, supporting both Wi-Fi and BLE wireless connectivities.
